// Logisim project cpu.circ as structural Verilog: 1 circuit, main circuit main
module main (
  input  CLK_RUN,
  input  [7:0] in_2,
  input  [15:0] in_3,
  input  in_4,
  input  in_5,
  output [3:0] out_6,
  output [7:0] out_7,
  output [15:0] out_8,
  output [15:0] out_9,
  output [7:0] out_10,
  output [7:0] out_11,
  output [15:0] out_12,
  output [7:0] out_13,
  output [7:0] out_14,
  output [7:0] out_15,
  output [7:0] L_Register,
  output [7:0] out_17,
  output [15:0] out_18,
  output [7:0] _C_Z,
  output [7:0] out_20,
  output [15:0] out_21,
  output [7:0] out_22,
  output [15:0] out_23,
  output [7:0] out_24,
  output [7:0] out_25
);

  wire A_TO_DATA, A_TO_X, adder_1_cout, ADDR_HI_TO_DATA, ADDR_LO_TO_DATA, ADDR_TO_HL, ADDR_TO_IP,
       ADDR_TO_MAR, ADDR_TO_SP, ADDR_TO_T, and_1_out, and_2_out, and_4_out, and_5_out, and_6_out, and_7_out,
       and_8_out, and_9_out, and_10_out, and_11_out, B_TO_DATA, C_TO_DATA, CLK, CLK_STEP_out, clock_1_out,
       D_TO_DATA, DATA_TO_A, DATA_TO_ADDR_HI, DATA_TO_ADDR_LO, DATA_TO_B, DATA_TO_C, DATA_TO_D, DATA_TO_IR,
       DATA_TO_MDR, DATA_TO_Y, FLAGS, H_TO_DATA, HL_TO_ADDR, HLT, HRST_out, IP_INC, IP_TO_ADDR, L_TO_DATA,
       MAR_INC, MDR_TO_DATA, minus_CLK, nor_1_out, not_1_out, not_2_out, not_3_out, not_5_out, NXT, or_2_out,
       or_3_out, or_4_out, or_5_out, or_6_out, or_7_out, or_8_out, or_9_out, or_10_out, or_11_out, or_12_out,
       RST, SP_DEC, SP_INC, SP_TO_ADDR, SRST, SUB, T_TO_ADDR, Z_TO_DATA;
  wire [2:0] rom_2_data, rom_2_data_2, rom_3_data_3;
  wire [2:2] rom_3_data;
  wire [7:0] bit_extender_1_out, xor_1_out;
  wire [7:6] rom_2_data_3, rom_3_data_2;

  Button CLK_STEP (.out(CLK_STEP_out));
  Button HRST (.out(HRST_out));
  Clock clock_1 (.out(clock_1_out));
  and and_1 (and_1_out, clock_1_out, CLK_RUN);
  not not_1 (not_1_out, CLK_RUN);
  and and_2 (and_2_out, not_1_out, CLK_STEP_out);
  or or_1 (RST, HRST_out, SRST);
  not not_2 (not_2_out, NXT);
  or or_2 (or_2_out, and_1_out, and_2_out);
  not not_3 (not_3_out, HLT);
  Demultiplexer #(.select(3)) demultiplexer_1 (
    .out1(DATA_TO_A), .out2(DATA_TO_B), .out3(DATA_TO_C), .out4(DATA_TO_D), .out5(DATA_TO_MDR),
    .out6(DATA_TO_ADDR_HI), .out7(DATA_TO_ADDR_LO), .in(1'b1), .sel(rom_2_data), .en(1'b1));  // open: out0
  Counter #(.width(4), .max('hf)) counter_1 (
    .load(NXT), .D(4'b0000), .count(not_2_out), .Q(out_6), .clk(minus_CLK), .clr(RST));  // open: carry
  not not_4 (minus_CLK, CLK);
  and and_3 (CLK, or_2_out, not_3_out);
  assign bit_extender_1_out = {{7{SUB}}, SUB};  // Bit_Extender bit_extender_1
  ROM #(.addrWidth(15)) rom_1 (
    .addr({1'b0, _C_Z[1:0], out_6, out_10}),
    .data({Z_TO_DATA, FLAGS, SUB, DATA_TO_Y, A_TO_X, NXT, SRST, HLT}), .sel(1'b1));
  Register register_1 (.D(out_7), .en(DATA_TO_IR), .Q(out_10), .clk(CLK), .clr(RST));
  Register register_2 (.D(out_7), .en(DATA_TO_A), .Q(out_11), .clk(CLK));  // open: clr
  Register register_3 (.D(out_11), .en(A_TO_X), .Q(out_13), .clk(CLK));  // open: clr
  assign xor_1_out = bit_extender_1_out ^ out_20;  // XOR_Gate xor_1, 8 bits wide
  Register register_4 (.D(out_7), .en(DATA_TO_Y), .Q(out_20), .clk(CLK));  // open: clr
  Register register_5 (.D(out_7), .en(DATA_TO_B), .Q(out_22), .clk(CLK));  // open: clr
  Register register_6 (.D(out_7), .en(DATA_TO_C), .Q(out_24), .clk(CLK));  // open: clr
  Register register_7 (.D(out_7), .en(DATA_TO_D), .Q(out_25), .clk(CLK));  // open: clr
  assign out_7 = A_TO_DATA ? out_11 : 8'bz;  // Controlled_Buffer controlled_buffer_1
  Adder adder_1 (.a(out_13), .b(xor_1_out), .out(out_14), .cin(SUB), .cout(adder_1_cout));
  assign out_7 = Z_TO_DATA ? out_14 : 8'bz;  // Controlled_Buffer controlled_buffer_2
  nor nor_1 (nor_1_out, out_14[0], out_14[1], out_14[2], out_14[3], out_14[4], out_14[5], out_14[6], out_14[7]);
  D_Flip_Flop d_ff_1 (.clk(CLK), .D(nor_1_out), .Q(_C_Z[0]), .en(FLAGS), .reset(RST));  // open: Qn, preset
  D_Flip_Flop d_ff_2 (.clk(CLK), .D(adder_1_cout), .Q(_C_Z[1]), .en(FLAGS), .reset(RST));  // open: Qn, preset
  assign out_7 = B_TO_DATA ? out_22 : 8'bz;  // Controlled_Buffer controlled_buffer_3
  assign out_7 = C_TO_DATA ? out_24 : 8'bz;  // Controlled_Buffer controlled_buffer_4
  assign out_7 = D_TO_DATA ? out_25 : 8'bz;  // Controlled_Buffer controlled_buffer_5
  Demultiplexer #(.select(3)) demultiplexer_2 (
    .out1(A_TO_DATA), .out2(B_TO_DATA), .out3(C_TO_DATA), .out4(D_TO_DATA), .out5(MDR_TO_DATA),
    .out6(ADDR_HI_TO_DATA), .out7(ADDR_LO_TO_DATA), .in(1'b1), .sel(rom_2_data_2), .en(1'b1));  // open: out0
  ROM #(.addrWidth(15)) rom_2 (
    .addr({1'b0, _C_Z[1:0], out_6, out_10}), .data({rom_2_data_3, rom_2_data_2, rom_2_data}), .sel(1'b1));
  assign out_7 = in_4 ? in_2 : 8'bz;  // Controlled_Buffer controlled_buffer_6
  assign out_7 = MDR_TO_DATA ? out_15 : 8'bz;  // Controlled_Buffer controlled_buffer_7
  assign out_7 = L_TO_DATA ? L_Register : 8'bz;  // Controlled_Buffer controlled_buffer_8
  assign out_7 = H_TO_DATA ? out_17 : 8'bz;  // Controlled_Buffer controlled_buffer_9
  not not_5 (not_5_out, DATA_TO_MDR);
  assign out_15 = DATA_TO_MDR ? out_7 : 8'bz;  // Controlled_Buffer controlled_buffer_10
  assign out_8[7:0] = DATA_TO_ADDR_LO ? out_7 : 8'bz;  // Controlled_Buffer controlled_buffer_11
  assign out_8[15:8] = DATA_TO_ADDR_HI ? out_7 : 8'bz;  // Controlled_Buffer controlled_buffer_12
  Demultiplexer #(.select(3)) demultiplexer_3 (
    .out1(ADDR_TO_IP), .out2(ADDR_TO_HL), .out3(ADDR_TO_T), .out4(ADDR_TO_SP), .out5(MAR_INC),
    .out6(ADDR_TO_MAR), .out7(DATA_TO_IR), .in(1'b1), .sel({rom_3_data[2], rom_2_data_3}), .en(1'b1));  // open: out0
  ROM #(.addrWidth(15)) rom_3 (
    .addr({1'b0, _C_Z[1:0], out_6, out_10}),
    .data({rom_3_data_2, L_TO_DATA, H_TO_DATA, rom_3_data_3, rom_3_data[2]}), .sel(1'b1));
  or or_3 (or_3_out, ADDR_TO_SP, SP_DEC);
  or or_4 (or_4_out, SP_DEC, SP_INC);
  Counter #(.width(16), .max('hffff)) counter_2 (
    .load(ADDR_TO_IP), .D(out_8), .count(IP_INC), .Q(out_9), .clk(CLK), .clr(RST));  // open: carry
  Counter #(.width(16), .max('hffff)) counter_3 (
    .load(ADDR_TO_MAR), .D(out_8), .count(MAR_INC), .Q(out_12), .clk(CLK));  // open: carry, clr
  Register #(.width(16)) register_8 (.D(out_8), .en(ADDR_TO_HL), .Q({out_17, L_Register}), .clk(CLK));  // open: clr
  Register #(.width(16)) register_9 (.D(out_8), .en(ADDR_TO_T), .Q(out_21), .clk(CLK));  // open: clr
  Counter #(.width(16), .max('hffff)) counter_4 (
    .load(or_3_out), .D(out_8), .count(or_4_out), .Q(out_23), .clk(CLK), .clr(RST));  // open: carry
  Demultiplexer #(.select(3)) demultiplexer_4 (
    .out1(IP_TO_ADDR), .out2(HL_TO_ADDR), .out3(T_TO_ADDR), .out4(SP_TO_ADDR), .out5(IP_INC), .out6(SP_INC),
    .out7(SP_DEC), .in(1'b1), .sel(rom_3_data_3), .en(1'b1));  // open: out0
  and and_4 (and_4_out, ADDR_TO_IP, DATA_TO_ADDR_HI);
  and and_5 (and_5_out, ADDR_TO_IP, DATA_TO_ADDR_LO);
  RAM #(.addrWidth(16)) ram_1 (.addr(out_12), .data(out_15), .sel(1'b1), .clk(CLK), .ld(not_5_out));  // open: clr
  and and_6 (and_6_out, ADDR_TO_HL, DATA_TO_ADDR_HI);
  and and_7 (and_7_out, ADDR_TO_HL, DATA_TO_ADDR_LO);
  and and_8 (and_8_out, ADDR_TO_T, DATA_TO_ADDR_HI);
  and and_9 (and_9_out, ADDR_TO_T, DATA_TO_ADDR_LO);
  and and_10 (and_10_out, ADDR_TO_SP, DATA_TO_ADDR_HI);
  and and_11 (and_11_out, ADDR_TO_SP, DATA_TO_ADDR_LO);
  assign out_8[7:0] = or_5_out ? out_9[7:0] : 8'bz;  // Controlled_Buffer controlled_buffer_13
  assign out_8[15:8] = or_6_out ? out_9[15:8] : 8'bz;  // Controlled_Buffer controlled_buffer_14
  or or_5 (or_5_out, and_4_out, IP_TO_ADDR);
  or or_6 (or_6_out, IP_TO_ADDR, and_5_out);
  assign out_8[7:0] = or_7_out ? L_Register : 8'bz;  // Controlled_Buffer controlled_buffer_15
  assign out_8[15:8] = or_8_out ? out_17 : 8'bz;  // Controlled_Buffer controlled_buffer_16
  or or_7 (or_7_out, and_6_out, HL_TO_ADDR);
  or or_8 (or_8_out, HL_TO_ADDR, and_7_out);
  assign out_8[7:0] = or_9_out ? out_21[7:0] : 8'bz;  // Controlled_Buffer controlled_buffer_17
  assign out_8[15:8] = or_10_out ? out_21[15:8] : 8'bz;  // Controlled_Buffer controlled_buffer_18
  or or_9 (or_9_out, and_8_out, T_TO_ADDR);
  or or_10 (or_10_out, T_TO_ADDR, and_9_out);
  assign out_8[7:0] = or_11_out ? out_23[7:0] : 8'bz;  // Controlled_Buffer controlled_buffer_19
  assign out_8[15:8] = or_12_out ? out_23[15:8] : 8'bz;  // Controlled_Buffer controlled_buffer_20
  or or_11 (or_11_out, and_10_out, SP_TO_ADDR);
  or or_12 (or_12_out, SP_TO_ADDR, and_11_out);
  assign out_7 = ADDR_LO_TO_DATA ? out_8[7:0] : 8'bz;  // Controlled_Buffer controlled_buffer_21
  assign out_7 = ADDR_HI_TO_DATA ? out_8[15:8] : 8'bz;  // Controlled_Buffer controlled_buffer_22
  assign out_8 = in_5 ? in_3 : 16'bz;  // Controlled_Buffer controlled_buffer_23

  assign _C_Z[7:2] = {6{1'b0}};
  assign out_18 = {out_17, L_Register};

  // Other names for the same wires on the sheet: ZF = _C_Z[0]; CF = _C_Z[1]

  // Notes on the sheet:
  //   Microsequencer
  //   Clock
  //   A Register
  //   X Register
  //   Y Register
  //   B Register
  //   C Register
  //   D Register
  //   Instruction Register
  //   0-7
  //   Adder / Subtractor
  //   Flags
  //   8-15
  //   8-Bit Data Bus
  //   Z Register
  //   16-23
  //   Memory Address Register
  //   H Register
  //   Instruction Pointer
  //   Memory Data Register
  //   HL Register
  //   T Register
  //   Stack Pointer
  //   16-Bit Address Bus
endmodule
